# Fritzing sketch SmartFreezer (saved by Fritzing 0.9.4)
breadboards: 1

parts:
  Componente1 = Bluetooth HC-05 Macho
  U2 = LCD-16X2 [package=lcd-16x2_nosilk]
  LCM1602_IIC1 = LCM1602 IIC [part_number="LCM1602 IIC" chip_label="LCM1602 IIC" package="DIP (Dual Inline) [THT]"]
  Componente2 = Arduino Uno (Rev3) - ICSP
  F1 = Fan - Ventilador [package=THT]
  F2 = Fan - Ventilador [package=THT]
  U4 = 2-Channel 5v Relay Shield [package=relay-2ch5v10a]
  Componente3 = Real Time Clock Module - DS1307 RTC Breakout Board
  DS1 = DS18B20 1-Wire Temperature Sensor [part_number=DS18B20]
  J5 = Peltier Element
  J6 = Peltier Element
  J8 = Power Jack [package=power_jack_smd]
  R1 = Resistor [tolerance=±5% resistance=3.3k package=THT]
  R2 = Resistor [tolerance=±5% resistance=3.3 package="0402 [SMD]"]
  Componente4 = Arduino Uno (Rev3) - ICSP  # not connected

nets:
  N1: Componente1.TXD, Componente2.D10_PWM/SS
  N2: Componente1.RXD, R1.Pin_0, R2.Pin_0
  VCC: Componente1.VCC, LCM1602_IIC1.VCC, Componente2.5V, U4.VCC, DS1.VDD
  GND: Componente1.GND, LCM1602_IIC1.GND, Componente2.GND, U4.GND, Componente3.GND, DS1.GND, R1.Pin_1
  VSS: U2.VSS, LCM1602_IIC1.VSS
  VDD: U2.VDD, LCM1602_IIC1.VDD
  N3: U2.VO, LCM1602_IIC1.V0
  N4: U2.RS, LCM1602_IIC1.RS
  N5: U2.R_W, LCM1602_IIC1.RW
  N6: U2.E, LCM1602_IIC1.E
  N7: U2.DB0, LCM1602_IIC1.D0
  N8: U2.DB1, LCM1602_IIC1.D1
  N9: U2.DB2, LCM1602_IIC1.D2
  N10: U2.DB3, LCM1602_IIC1.D3
  N11: U2.DB4, LCM1602_IIC1.D4
  N12: U2.DB5, LCM1602_IIC1.D5
  N13: U2.DB6, LCM1602_IIC1.D6
  N14: U2.DB7, LCM1602_IIC1.D7
  N15: U2.A, LCM1602_IIC1.A
  N16: U2.K, LCM1602_IIC1.K
  N17: LCM1602_IIC1.SDA, Componente2.A4/SDA, Componente3.SDA
  N18: LCM1602_IIC1.SCL, Componente2.A5/SCL, Componente3.SCL
  N19: LCM1602_IIC1.LED_A, LCM1602_IIC1.LED_B
  N20: Componente2.A0, DS1.DQ
  N21: Componente2.D11_PWM/MOSI, R2.Pin_1
  N22: Componente2.D12/MISO, U4.IN2
  N23: Componente2.D13/SCK, U4.IN1
  3V3: Componente2.3V3, Componente3.5V
  N24: F1.5V, U4.K2-On
  GND_2: F1.GND, F2.GND, J6.pin1, J8.GND
  N25: F2.5V, U4.K1-On, J5.pin2
  N26: U4.K1-In, U4.K2-In, J8.GNDBREAK

notes:
  Placas Peltier
  Coolers de resfriamento e circulação de ar
  Shield Rele 2 canais
  Modulo Bluetooth
  Modulo LCD + Modulo I2C com ajuste manual de brilho
  Sensor temperatura DS18B20
  Modulo Relógio RTC DS1307
  Arduino Uno

custom parts:
  LCM1602 IIC: I2C-Module to use a 1602 or 2004 LCD on with the wire.h libory Serial LCD Modul
  Fan - Ventilador: Ventilador de 2 pines, se encuentra comunmente en computadoras de escritorio
  2-Channel 5v Relay Shield: 2 Channel 5v Relay Shield w. 2x SPD-06VDC-SD-C
